// Logisim project hw3.circ as structural Verilog: 4 circuits, main circuit 16-bit ALU
module _1_bit_Full_Adder (
  input  A,
  input  B,
  input  CarryIn,
  output Answer,
  output CarryOut
);

  wire and_1_out, and_2_out, xor_1_out;

  xor xor_1 (xor_1_out, A, B);
  and and_1 (and_1_out, A, B);
  xor xor_2 (Answer, xor_1_out, CarryIn);
  and and_2 (and_2_out, xor_1_out, CarryIn);
  or or_1 (CarryOut, and_2_out, and_1_out);
endmodule

module _4_bit_Full_Adder (
  input  [3:0] A,
  input  [3:0] B,
  input  CarryIn,
  output CarryOut,
  output [3:0] Answer
);

  wire n1_bit_full_adder_1_carryout, n1_bit_full_adder_2_carryout, n1_bit_full_adder_3_carryout;

  _1_bit_Full_Adder u_1_bit_full_adder_1 (
    .A(A[0]), .B(B[0]), .CarryIn(CarryIn), .Answer(Answer[0]), .CarryOut(n1_bit_full_adder_1_carryout));
  _1_bit_Full_Adder u_1_bit_full_adder_2 (
    .A(A[1]), .B(B[1]), .CarryIn(n1_bit_full_adder_1_carryout), .Answer(Answer[1]),
    .CarryOut(n1_bit_full_adder_2_carryout));
  _1_bit_Full_Adder u_1_bit_full_adder_3 (
    .A(A[2]), .B(B[2]), .CarryIn(n1_bit_full_adder_2_carryout), .Answer(Answer[2]),
    .CarryOut(n1_bit_full_adder_3_carryout));
  _1_bit_Full_Adder u_1_bit_full_adder_4 (
    .A(A[3]), .B(B[3]), .CarryIn(n1_bit_full_adder_3_carryout), .Answer(Answer[3]), .CarryOut(CarryOut));
endmodule

module _4_bit_ALU (
  input  in_1,
  input  in_2,
  input  [3:0] A,
  input  [3:0] B,
  input  S2,
  input  S1,
  input  S0,
  output Addition,
  output out_9,
  output Increment,
  output Negation,
  output [3:0] out_12,
  output out_13
);

  wire [3:0] AND_out, n4_bit_full_adder_1_answer, n4_bit_full_adder_2_answer, n4_bit_full_adder_3_answer,
       n4_bit_full_adder_4_answer, n4_bit_full_adder_5_answer, not_1_out, not_2_out, NOT_3_out, OR_out,
       XOR_out;

  assign not_1_out = ~B;  // NOT_Gate not_1, 4 bits wide
  _4_bit_Full_Adder u_4_bit_full_adder_1 (
    .A(A), .B(B), .CarryIn(in_1), .CarryOut(Addition), .Answer(n4_bit_full_adder_1_answer));
  assign not_2_out = ~A;  // NOT_Gate not_2, 4 bits wide
  assign AND_out = A & B;  // AND_Gate AND, 4 bits wide
  assign OR_out = A | B;  // OR_Gate OR, 4 bits wide
  assign NOT_3_out = ~A;  // NOT_Gate NOT_3, 4 bits wide
  assign XOR_out = A ^ B;  // XOR_Gate XOR, 4 bits wide
  _4_bit_Full_Adder u_4_bit_full_adder_2 (
    .A(not_1_out), .B(4'b0001), .CarryIn(1'b0), .CarryOut(Increment), .Answer(n4_bit_full_adder_2_answer));
  _4_bit_Full_Adder u_4_bit_full_adder_3 (
    .A(A), .B(4'b0001), .CarryIn(1'b0), .CarryOut(Negation), .Answer(n4_bit_full_adder_3_answer));
  _4_bit_Full_Adder u_4_bit_full_adder_4 (
    .A(not_2_out), .B(4'b0001), .CarryIn(1'b0), .CarryOut(out_13), .Answer(n4_bit_full_adder_4_answer));
  _4_bit_Full_Adder u_4_bit_full_adder_5 (
    .A(A), .B(n4_bit_full_adder_2_answer), .CarryIn(in_2), .CarryOut(out_9),
    .Answer(n4_bit_full_adder_5_answer));
  Multiplexer #(.select(3), .width(4), .disabled(0), .enable("false")) multiplexer_1 (
    .in0(n4_bit_full_adder_1_answer), .in1(n4_bit_full_adder_5_answer), .in2(n4_bit_full_adder_3_answer),
    .in3(n4_bit_full_adder_4_answer), .in4(AND_out), .in5(OR_out), .in6(NOT_3_out), .in7(XOR_out),
    .out(out_12), .sel({S2, S1, S0}));

  // Notes on the sheet:
  //   Subtraction
  //   op-codes
  //   0 0 0 Addition
  //   0 0 1 Subtraction
  //   0 1 0  Incresment
  //   0 1 1 Negation
  //   1 0 0 AND
  //   1 0 1 OR
  //   1 1 0 NOT
  //   1 1 1 XOR
endmodule

module _16_bit_ALU (
  input  [15:0] in_1,
  input  [15:0] in_2,
  input  in_3,
  input  S2,
  input  S1,
  input  in_6,
  output [15:0] out_7
);

  wire n4_bit_alu_1_addition, n4_bit_alu_2_addition, n4_bit_alu_3_addition;

  _4_bit_ALU u_4_bit_alu_1 (
    .in_1(in_3), .A(in_1[3:0]), .B(in_2[3:0]), .Addition(n4_bit_alu_1_addition), .out_12(out_7[3:0]),
    .S2(S2), .S1(S1), .S0(in_6));  // open: in_2, out_9, Increment, Negation, out_13
  _4_bit_ALU u_4_bit_alu_2 (
    .in_1(n4_bit_alu_1_addition), .A(in_1[7:4]), .B(in_2[7:4]), .Addition(n4_bit_alu_2_addition),
    .out_12(out_7[7:4]), .S2(S2), .S1(S1), .S0(in_6));  // open: in_2, out_9, Increment, Negation, out_13
  _4_bit_ALU u_4_bit_alu_3 (
    .in_1(n4_bit_alu_2_addition), .A(in_1[11:8]), .B(in_2[11:8]), .Addition(n4_bit_alu_3_addition),
    .out_12(out_7[11:8]), .S2(S2), .S1(S1), .S0(in_6));  // open: in_2, out_9, Increment, Negation, out_13
  _4_bit_ALU u_4_bit_alu_4 (
    .in_1(n4_bit_alu_3_addition), .A(in_1[15:12]), .B(in_2[15:12]), .out_12(out_7[15:12]), .S2(S2), .S1(S1),
    .S0(in_6));  // open: in_2, Addition, out_9, Increment, Negation, out_13

  // Notes on the sheet:
  //   S0
  //   0 0 0 Addition
  //   0 0 1 Subtraction
  //   0 1 0  Increasment
  //   0 1 1 Negation
  //   1 0 0 AND
  //   1 0 1 OR
  //   1 1 0 NOT
  //   1 1 1 XOR
endmodule
