// Logisim project hw4part2.circ as structural Verilog: 2 circuits, main circuit One-Hot State Machine
module Tester (
  input  G
);

  wire Clock_out, one_hot_state_machine_1_w, one_hot_state_machine_1_x, one_hot_state_machine_1_y,
       one_hot_state_machine_1_z, Reset_out;

  One_Hot_State_Machine one_hot_state_machine_1 (
    .W(one_hot_state_machine_1_w), .Clock(Clock_out), .Reset(Reset_out), .G(G),
    .X(one_hot_state_machine_1_x), .Y(one_hot_state_machine_1_y), .Z(one_hot_state_machine_1_z));
  Clock Clock (.out(Clock_out));
  LED W (.in(one_hot_state_machine_1_w));
  LED X (.in(one_hot_state_machine_1_x));
  LED Y (.in(one_hot_state_machine_1_y));
  LED Z (.in(one_hot_state_machine_1_z));
  Button Reset (.out(Reset_out));

  // Notes on the sheet:
  //   You can use this to test your circuit.
endmodule

module One_Hot_State_Machine (
  input  G,
  input  Clock,
  input  Reset,
  output W,
  output X,
  output Y,
  output Z
);

  wire and_1_out, and_5_out, and_6_out, and_7_out, and_8_out, CS0, CS1, CS2, CS3, CS4, CS5, nor_1_out, NS0,
       NS1, NS2, NS3, NS4, NS5, NS6;

  nor nor_1 (nor_1_out, CS0, CS1, CS2, CS3, CS4, CS5, W);
  and and_1 (and_1_out, CS0, ~G);  // AND_Gate
  and and_2 (NS1, CS0, G);
  and and_3 (NS2, CS1, G);
  and and_4 (NS4, CS1, G);
  Register #(.width(7)) register_1 (
    .D({NS6, NS5, NS4, NS3, NS2, NS1, NS0}), .Q({W, CS5, CS4, CS3, CS2, CS1, CS0}), .clk(Clock), .clr(Reset));  // open: en
  or or_1 (NS0, nor_1_out, and_1_out, W);
  and and_5 (and_5_out, CS3, ~G);  // AND_Gate
  and and_6 (and_6_out, CS5, G);
  or or_2 (NS3, CS2, and_5_out);
  or or_3 (NS5, CS4, and_6_out);
  or or_4 (X, CS0, CS1, CS3);
  or or_5 (Y, CS3, CS4);
  or or_6 (Z, CS1, CS2, CS4, W);
  and and_7 (and_7_out, CS5, ~G);  // AND_Gate
  and and_8 (and_8_out, CS3, G);
  or or_7 (NS6, and_7_out, and_8_out);

  // Other names for the same wires on the sheet: CLK = Clock; RST = Reset;
  //   Start[6:0] = {W, CS5, CS4, CS3, CS2, CS1, CS0}; CS6 = W

  // Notes on the sheet:
  //   My name is
  //   [Jongyeon Kim]
  //   and this is my pretty one-hot state machine!
endmodule
